// Logisim project control_logic.circ as structural Verilog: 1 circuit, main circuit control_logic
module control_logic (
  input  [31:0] inst,
  input  BrEq,
  input  BrLt,
  output PCSel,
  output RegWEn,
  output [2:0] ImmSel,
  output BrUn,
  output ASel,
  output BSel,
  output [3:0] ALUSel,
  output MemRW,
  output [1:0] WBSel,
  output CSRSel,
  output CSRWen
);

  wire and_9_out, BranchCond, comparator_3_eq, comparator_7_eq, comparator_8_eq, comparator_9_eq,
       comparator_10_eq, comparator_12_eq, comparator_13_eq, isAUIPC, isBranch, isCSROpcode, isCSRW, isF3_0,
       isF3_5, isF7_20, isI_ALU, isJAL, isJALR, isJump, isLoadOpcode, isLUI, isLW, isMemAccess, isMGroup,
       isR, isSraFamily, isStoreOpcode, isSub, isUType, isWordFunct3, isX20Group, not_1_out, not_2_out,
       or_1_out, or_12_out, UnsignedBranchCode;
  wire [1:0] multiplexer_8_out;
  wire [2:0] multiplexer_7_out, multiplexer_9_out, multiplexer_12_out;
  wire [3:0] BaseALUSel, M_ALUSel, multiplexer_6_out, multiplexer_11_out, multiplexer_13_out, U_ALUSel,
       X20_ALUSel;

  or or_1 (or_1_out, isR, isI_ALU);
  not not_1 (not_1_out, BrEq);
  not not_2 (not_2_out, BrLt);
  Comparator #(.width(7)) comparator_1 (.a(inst[6:0]), .b(7'b0010011), .eq(isI_ALU));  // open: gt, lt
  Comparator #(.width(7)) comparator_2 (.a(inst[6:0]), .b(7'b0110011), .eq(isR));  // open: gt, lt
  Comparator #(.width(7)) comparator_3 (.a(inst[31:25]), .b(7'b0000001), .eq(comparator_3_eq));  // open: gt, lt
  Comparator #(.width(7)) comparator_4 (.a(7'b0100000), .b(inst[31:25]), .eq(isF7_20));  // open: gt, lt
  Comparator #(.width(3)) comparator_5 (.a(3'b000), .b(inst[14:12]), .eq(isF3_0));  // open: gt, lt
  Comparator #(.width(3)) comparator_6 (.a(3'b101), .b(inst[14:12]), .eq(isF3_5));  // open: gt, lt
  Comparator #(.width(3)) comparator_7 (.a(3'b110), .b(inst[14:12]), .eq(comparator_7_eq));  // open: gt, lt
  Comparator #(.width(3)) comparator_8 (.a(3'b111), .b(inst[14:12]), .eq(comparator_8_eq));  // open: gt, lt
  Comparator #(.width(7)) comparator_9 (.a(7'b1100111), .b(inst[6:0]), .eq(comparator_9_eq));  // open: gt, lt
  Comparator #(.width(3)) comparator_10 (.a(3'b000), .b(inst[14:12]), .eq(comparator_10_eq));  // open: gt, lt
  Comparator #(.width(7)) comparator_11 (.a(7'b1110011), .b(inst[6:0]), .eq(isCSROpcode));  // open: gt, lt
  Comparator #(.width(3)) comparator_12 (.a(3'b001), .b(inst[14:12]), .eq(comparator_12_eq));  // open: gt, lt
  Comparator #(.width(3)) comparator_13 (.a(3'b101), .b(inst[14:12]), .eq(comparator_13_eq));  // open: gt, lt
  Multiplexer #(.enable("false"), .select(3), .width(4)) multiplexer_1 (
    .in0(4'b0000), .in1(4'b0110), .in2(4'b0111), .in3(4'b0000), .in4(4'b0011), .in5(4'b0100), .in6(4'b0010),
    .in7(4'b0001), .out(BaseALUSel), .sel(inst[14:12]));
  Multiplexer #(.enable("false"), .select(3), .width(4)) multiplexer_2 (
    .in0(4'b1010), .in1(4'b1110), .in2(4'b0000), .in3(4'b1011), .in4(4'b0000), .in5(4'b0000), .in6(4'b0000),
    .in7(4'b0000), .out(M_ALUSel), .sel(inst[14:12]));
  and and_1 (isSub, isF3_0, isF7_20, isR);
  and and_2 (isSraFamily, isF3_5, isF7_20, or_1_out);
  or or_2 (isX20Group, isSraFamily, isSub);
  Multiplexer #(.enable("false"), .select(3), .width(4)) multiplexer_3 (
    .in0(4'b1100), .in1(4'b0000), .in2(4'b0000), .in3(4'b0000), .in4(4'b0000), .in5(4'b0101), .in6(4'b0000),
    .in7(4'b0000), .out(X20_ALUSel), .sel(inst[14:12]));
  Comparator #(.width(7)) comparator_14 (.a(inst[6:0]), .b(7'b0110111), .eq(isLUI));  // open: gt, lt
  Comparator #(.width(7)) comparator_15 (.a(inst[6:0]), .b(7'b0010111), .eq(isAUIPC));  // open: gt, lt
  or or_3 (isUType, isLUI, isAUIPC);
  Multiplexer #(.enable("false"), .width(4)) multiplexer_4 (.in0(4'b0000), .in1(4'b1101), .out(U_ALUSel), .sel(isLUI));
  Comparator #(.width(7)) comparator_16 (.a(7'b0000011), .b(inst[6:0]), .eq(isLoadOpcode));  // open: gt, lt
  Comparator #(.width(3)) comparator_17 (.a(3'b010), .b(inst[14:12]), .eq(isWordFunct3));  // open: gt, lt
  and and_3 (isLW, isLoadOpcode, isWordFunct3);
  Comparator #(.width(7)) comparator_18 (.a(7'b0100011), .b(inst[6:0]), .eq(isStoreOpcode));  // open: gt, lt
  and and_4 (MemRW, isStoreOpcode, isWordFunct3);
  or or_4 (isMemAccess, isLW, MemRW);
  Comparator #(.width(7)) comparator_19 (.a(7'b1100011), .b(inst[6:0]), .eq(isBranch));  // open: gt, lt
  or or_5 (UnsignedBranchCode, comparator_7_eq, comparator_8_eq);
  Multiplexer #(.enable("false"), .select(3)) multiplexer_5 (
    .in0(BrEq), .in1(not_1_out), .in2(1'b0), .in3(1'b0), .in4(BrLt), .in5(not_2_out), .in6(BrLt),
    .in7(not_2_out), .out(BranchCond), .sel(inst[14:12]));
  Comparator #(.width(7)) comparator_20 (.a(7'b1101111), .b(inst[6:0]), .eq(isJAL));  // open: gt, lt
  or or_6 (isJump, isJAL, isJALR);
  and and_5 (isMGroup, isR, comparator_3_eq);
  and and_6 (isJALR, comparator_9_eq, comparator_10_eq);
  and and_7 (isCSRW, isCSROpcode, comparator_12_eq);
  and and_8 (CSRSel, isCSROpcode, comparator_13_eq);
  Multiplexer #(.enable("false"), .width(4)) multiplexer_6 (
    .in0(BaseALUSel), .in1(X20_ALUSel), .out(multiplexer_6_out), .sel(isX20Group));
  Multiplexer #(.enable("false"), .width(3)) multiplexer_7 (
    .in0(3'b000), .in1(3'b011), .out(multiplexer_7_out), .sel(isUType));
  Multiplexer #(.enable("false"), .width(2)) multiplexer_8 (
    .in0(2'b00), .in1(2'b01), .out(multiplexer_8_out), .sel(isLW));
  and and_9 (and_9_out, BranchCond, isBranch);
  or or_7 (CSRWen, isCSRW, CSRSel);
  Multiplexer #(.enable("false"), .width(3)) multiplexer_9 (
    .in0(multiplexer_7_out), .in1(3'b001), .out(multiplexer_9_out), .sel(MemRW));
  or or_8 (RegWEn, isR, isI_ALU, isUType, isLW, isJump);
  Multiplexer #(.enable("false"), .width(2)) multiplexer_10 (
    .in0(multiplexer_8_out), .in1(2'b10), .out(WBSel), .sel(isJump));
  or or_9 (PCSel, and_9_out, isJump);
  and and_10 (BrUn, UnsignedBranchCode, isBranch);
  Multiplexer #(.enable("false"), .width(4)) multiplexer_11 (
    .in0(multiplexer_6_out), .in1(M_ALUSel), .out(multiplexer_11_out), .sel(isMGroup));
  or or_10 (BSel, isI_ALU, isUType, isMemAccess, isBranch, isJump);
  Multiplexer #(.enable("false"), .width(3)) multiplexer_12 (
    .in0(multiplexer_9_out), .in1(3'b010), .out(multiplexer_12_out), .sel(isBranch));
  or or_11 (ASel, isAUIPC, isBranch, isJAL);
  Multiplexer #(.enable("false"), .width(4)) multiplexer_13 (
    .in0(multiplexer_11_out), .in1(U_ALUSel), .out(multiplexer_13_out), .sel(isUType));
  Multiplexer #(.enable("false"), .width(3)) multiplexer_14 (
    .in0(multiplexer_12_out), .in1(3'b100), .out(ImmSel), .sel(isJAL));
  Multiplexer #(.enable("false"), .width(4)) multiplexer_15 (
    .in0(multiplexer_13_out), .in1(4'b0000), .out(ALUSel), .sel(or_12_out));
  or or_12 (or_12_out, isMemAccess, isBranch, isJump);

  // Other names for the same wires on the sheet: opcode[6:0] = inst[6:0]; funct3[2:0] = inst[14:12];
  //   funct7[6:0] = inst[31:25]; isCSRWI = CSRSel; isSW = MemRW

  // Notes on the sheet:
  //   INPUTS to your circuit
  //   DON'T CHANGE THE LOCATIONS OF THE INPUTS AND OUTPUTS!
  //   OUTPUT from your circuit
endmodule
