// Logisim project cpu.circ as structural Verilog: 1 circuit, main circuit cpu
module cpu (
  input  clk,
  input  [31:0] INSTRUCTION,
  input  [31:0] READ_DATA,
  output [31:0] WRITE_ADDRESS,
  output [31:0] PROGRAM_COUNTER,
  output [31:0] ra,
  output [31:0] sp,
  output [31:0] t0,
  output [31:0] t1,
  output [31:0] t2,
  output [31:0] s0,
  output [31:0] s1,
  output [31:0] a0,
  output [31:0] tohost,
  output [3:0] WRITE_ENABLE,
  output [31:0] WRITE_DATA
);

  wire ASel, BrEq, BrLt, BrUn, Bsel, CSRSel, CSRWen, MemRW, PCSel, RegWEn;
  wire [1:0] WBSel;
  wire [2:0] ImmSel;
  wire [3:0] ALUSel;
  wire [4:0] rd, rs1;
  wire [11:0] CSRAddress;
  wire [14:0] register_1_q;
  wire [31:0] adder_1_out, CSR_UImm, imm, multiplexer_1_out, multiplexer_2_out, multiplexer_4_out,
       multiplexer_5_out, multiplexer_6_out, PC_X, PCPlus4_X, ReadData1, WriteBackData;

  Multiplexer #(.enable("false"), .width(32)) multiplexer_1 (
    .in0(adder_1_out), .in1(WRITE_ADDRESS), .out(multiplexer_1_out), .sel(PCSel));
  Adder #(.width(32)) adder_1 (.a(PROGRAM_COUNTER), .b(32'h4), .out(adder_1_out));  // open: cin, cout
  Register #(.width(32)) PC (.D(multiplexer_1_out), .clk(clk), .Q(PROGRAM_COUNTER));  // open: en, clr
  Register #(.width(32)) register_1 (
    .D(multiplexer_2_out), .en(1'b1), .clk(clk),
    .Q({CSRAddress, rs1, register_1_q[14:12], rd, register_1_q[6:0]}));  // open: clr
  Multiplexer #(.enable("false"), .width(32)) multiplexer_2 (
    .in0(INSTRUCTION), .in1({32{1'b0}}), .out(multiplexer_2_out), .sel(PCSel));
  Register #(.width(32)) register_2 (.D(PROGRAM_COUNTER), .en(1'b1), .clk(clk), .Q(PC_X));  // open: clr
  Adder #(.width(32)) adder_2 (.a(PC_X), .b(32'h4), .out(PCPlus4_X));  // open: cin, cout
  imm_gen imm_gen_1 (.inst({CSRAddress, rs1, register_1_q[14:12], rd, register_1_q[6:0]}), .ImmSel(ImmSel), .imm(imm));
  assign CSR_UImm = {{27{1'b0}}, rs1};  // Bit_Extender bit_extender_1
  control_logic control_logic_1 (
    .CSRWen(CSRWen), .PCSel(PCSel), .RegWEn(RegWEn), .ImmSel(ImmSel), .BrUn(BrUn), .ASel(ASel), .BSel(Bsel),
    .ALUSel(ALUSel), .MemRW(MemRW), .WBSel(WBSel), .CSRSel(CSRSel),
    .inst({CSRAddress, rs1, register_1_q[14:12], rd, register_1_q[6:0]}), .BrEq(BrEq), .BrLt(BrLt));
  Multiplexer #(.enable("false"), .select(2), .width(32)) multiplexer_3 (
    .in0(WRITE_ADDRESS), .in1(READ_DATA), .in2(PCPlus4_X), .in3({32{1'b0}}), .out(WriteBackData), .sel(WBSel));
  regfile regfile_1 (
    .rs1(rs1), .rs2(CSRAddress[4:0]), .rd(rd), .Write_Data(WriteBackData), .RegWEn(RegWEn), .clk(clk),
    .ra(ra), .sp(sp), .t0(t0), .t1(t1), .t2(t2), .s0(s0), .s1(s1), .a0(a0), .Read_Data_1(ReadData1),
    .Read_Data_2(WRITE_DATA));
  branch_comp branch_comp_1 (.rs1(ReadData1), .rs2(WRITE_DATA), .BrUn(BrUn), .BrEq(BrEq), .BrLt(BrLt));
  Multiplexer #(.enable("false"), .width(32)) multiplexer_4 (
    .in0(ReadData1), .in1(CSR_UImm), .out(multiplexer_4_out), .sel(CSRSel));
  Multiplexer #(.enable("false"), .width(32)) multiplexer_5 (
    .in0(ReadData1), .in1(PC_X), .out(multiplexer_5_out), .sel(ASel));
  Multiplexer #(.enable("false"), .width(32)) multiplexer_6 (
    .in0(WRITE_DATA), .in1(imm), .out(multiplexer_6_out), .sel(Bsel));
  alu alu_1 (.Result(WRITE_ADDRESS), .A(multiplexer_5_out), .B(multiplexer_6_out), .ALUSel(ALUSel));
  csr csr_1 (.CSR_address(CSRAddress), .CSR_din(multiplexer_4_out), .CSR_WE(CSRWen), .clk(clk), .tohost(tohost));
  Multiplexer #(.enable("false"), .width(4)) multiplexer_7 (
    .in0(4'b0000), .in1(4'b1111), .out(WRITE_ENABLE), .sel(MemRW));

  // Other names for the same wires on the sheet: rs2[4:0] = CSRAddress[4:0]; ALUres[31:0] = WRITE_ADDRESS;
  //   ReadData2[31:0] = WRITE_DATA

  // Notes on the sheet:
  //   bubble
  //   Output to IMEM
  //   IMEM (do **NOT** move this)
  //   Inputs from IMEM
  //   It is OK to move the PC, RegFile, ALU, MEM, Branch Comp, Imm Gen, and Control Logic to wherever is most convenient for you when constructing your CPU, and to delete this text
  //   Inputs/Outputs for testing. Do **NOT** move these.
  //   Outputs To DMEM
  //   DMEM (do **NOT** move this)
  //   Inputs From DMEM
endmodule
