// Logisim project csr.circ as structural Verilog: 1 circuit, main circuit csr
module csr (
  input  [11:0] CSR_address,
  input  [31:0] CSR_din,
  input  CSR_WE,
  input  clk,
  output [31:0] tohost
);

  wire isTohostAddress, TohostWE;

  Comparator #(.width(12)) comparator_1 (.a(CSR_address), .b(12'h51e), .eq(isTohostAddress));  // open: gt, lt
  and and_1 (TohostWE, isTohostAddress, CSR_WE);
  Register #(.width(32)) register_1 (.D(CSR_din), .en(TohostWE), .clk(clk), .Q(tohost));  // open: clr

  // Other names for the same wires on the sheet: address[11:0] = CSR_address; data[31:0] = CSR_din; WE = CSR_WE

  // Notes on the sheet:
  //   INPUTS to your circuit
  //   OUTPUT from your circuit
  //   DON'T CHANGE THE LOCATIONS OF THE INPUTS AND OUTPUTS!
endmodule
