// Logisim project regfile.circ as structural Verilog: 1 circuit, main circuit regfile
module regfile (
  input  [4:0] rs1,
  input  [4:0] rs2,
  input  [4:0] rd,
  input  [31:0] Write_Data,
  input  RegWEn,
  input  clk,
  output [31:0] ra,
  output [31:0] sp,
  output [31:0] t0,
  output [31:0] t1,
  output [31:0] t2,
  output [31:0] s0,
  output [31:0] s1,
  output [31:0] a0,
  output [31:0] Read_Data_1,
  output [31:0] Read_Data_2
);

  wire x1, x2, x3, x4, x5, x6, x7, x8, x9, x10, x11, x12, x13, x14, x15, x16, x17, x18, x19, x20, x21, x22,
       x23, x24, x25, x26, x27, x28, x29, x30, x31;
  wire [31:0] x0o, x3o, x4o, x11o, x12o, x13o, x14o, x15o, x16o, x17o, x18o, x19o, x20o, x21o, x22o, x23o,
       x24o, x25o, x26o, x27o, x28o, x29o, x30o, x31o;

  Register #(.width(32)) x0 (.en(1'b0), .clk(clk), .Q(x0o));  // open: D, clr
  Register #(.width(32)) u_x8 (.D(Write_Data), .en(x8), .clk(clk), .Q(s0));  // open: clr
  Register #(.width(32)) register_1 (.D(Write_Data), .en(x16), .clk(clk), .Q(x16o));  // open: clr
  Register #(.width(32)) register_2 (.D(Write_Data), .en(x24), .clk(clk), .Q(x24o));  // open: clr
  Register #(.width(32)) u_x1 (.D(Write_Data), .en(x1), .clk(clk), .Q(ra));  // open: clr
  Register #(.width(32)) u_x9 (.D(Write_Data), .en(x9), .clk(clk), .Q(s1));  // open: clr
  Register #(.width(32)) register_3 (.D(Write_Data), .en(x17), .clk(clk), .Q(x17o));  // open: clr
  Register #(.width(32)) register_4 (.D(Write_Data), .en(x25), .clk(clk), .Q(x25o));  // open: clr
  Register #(.width(32)) u_x2 (.D(Write_Data), .en(x2), .clk(clk), .Q(sp));  // open: clr
  Register #(.width(32)) u_x10 (.D(Write_Data), .en(x10), .clk(clk), .Q(a0));  // open: clr
  Register #(.width(32)) register_5 (.D(Write_Data), .en(x18), .clk(clk), .Q(x18o));  // open: clr
  Register #(.width(32)) register_6 (.D(Write_Data), .en(x26), .clk(clk), .Q(x26o));  // open: clr
  Demultiplexer #(.enable("false"), .select(5)) demultiplexer_1 (
    .out1(x1), .out2(x2), .out3(x3), .out4(x4), .out5(x5), .out6(x6), .out7(x7), .out8(x8), .out9(x9),
    .out10(x10), .out11(x11), .out12(x12), .out13(x13), .out14(x14), .out15(x15), .out16(x16), .out17(x17),
    .out18(x18), .out19(x19), .out20(x20), .out21(x21), .out22(x22), .out23(x23), .out24(x24), .out25(x25),
    .out26(x26), .out27(x27), .out28(x28), .out29(x29), .out30(x30), .out31(x31), .in(RegWEn), .sel(rd));  // open: out0
  Register #(.width(32)) u_x3 (.D(Write_Data), .en(x3), .clk(clk), .Q(x3o));  // open: clr
  Register #(.width(32)) u_x11 (.D(Write_Data), .en(x11), .clk(clk), .Q(x11o));  // open: clr
  Register #(.width(32)) register_7 (.D(Write_Data), .en(x19), .clk(clk), .Q(x19o));  // open: clr
  Register #(.width(32)) register_8 (.D(Write_Data), .en(x27), .clk(clk), .Q(x27o));  // open: clr
  Register #(.width(32)) u_x4 (.D(Write_Data), .en(x4), .clk(clk), .Q(x4o));  // open: clr
  Register #(.width(32)) u_x12 (.D(Write_Data), .en(x12), .clk(clk), .Q(x12o));  // open: clr
  Register #(.width(32)) register_9 (.D(Write_Data), .en(x20), .clk(clk), .Q(x20o));  // open: clr
  Register #(.width(32)) register_10 (.D(Write_Data), .en(x28), .clk(clk), .Q(x28o));  // open: clr
  Multiplexer #(.enable("false"), .select(5), .width(32)) multiplexer_1 (
    .in0(x0o), .in1(ra), .in2(sp), .in3(x3o), .in4(x4o), .in5(t0), .in6(t1), .in7(t2), .in8(s0), .in9(s1),
    .in10(a0), .in11(x11o), .in12(x12o), .in13(x13o), .in14(x14o), .in15(x15o), .in16(x16o), .in17(x17o),
    .in18(x18o), .in19(x19o), .in20(x20o), .in21(x21o), .in22(x22o), .in23(x23o), .in24(x24o), .in25(x25o),
    .in26(x26o), .in27(x27o), .in28(x28o), .in29(x29o), .in30(x30o), .in31(x31o), .out(Read_Data_1), .sel(rs1));
  Multiplexer #(.enable("false"), .select(5), .width(32)) multiplexer_2 (
    .in0(x0o), .in1(ra), .in2(sp), .in3(x3o), .in4(x4o), .in5(t0), .in6(t1), .in7(t2), .in8(s0), .in9(s1),
    .in10(a0), .in11(x11o), .in12(x12o), .in13(x13o), .in14(x14o), .in15(x15o), .in16(x16o), .in17(x17o),
    .in18(x18o), .in19(x19o), .in20(x20o), .in21(x21o), .in22(x22o), .in23(x23o), .in24(x24o), .in25(x25o),
    .in26(x26o), .in27(x27o), .in28(x28o), .in29(x29o), .in30(x30o), .in31(x31o), .out(Read_Data_2), .sel(rs2));
  Register #(.width(32)) u_x5 (.D(Write_Data), .en(x5), .clk(clk), .Q(t0));  // open: clr
  Register #(.width(32)) u_x13 (.D(Write_Data), .en(x13), .clk(clk), .Q(x13o));  // open: clr
  Register #(.width(32)) register_11 (.D(Write_Data), .en(x21), .clk(clk), .Q(x21o));  // open: clr
  Register #(.width(32)) register_12 (.D(Write_Data), .en(x29), .clk(clk), .Q(x29o));  // open: clr
  Register #(.width(32)) u_x6 (.D(Write_Data), .en(x6), .clk(clk), .Q(t1));  // open: clr
  Register #(.width(32)) u_x14 (.D(Write_Data), .en(x14), .clk(clk), .Q(x14o));  // open: clr
  Register #(.width(32)) register_13 (.D(Write_Data), .en(x22), .clk(clk), .Q(x22o));  // open: clr
  Register #(.width(32)) register_14 (.D(Write_Data), .en(x30), .clk(clk), .Q(x30o));  // open: clr
  Register #(.width(32)) u_x7 (.D(Write_Data), .en(x7), .clk(clk), .Q(t2));  // open: clr
  Register #(.width(32)) u_x15 (.D(Write_Data), .en(x15), .clk(clk), .Q(x15o));  // open: clr
  Register #(.width(32)) register_15 (.D(Write_Data), .en(x23), .clk(clk), .Q(x23o));  // open: clr
  Register #(.width(32)) register_16 (.D(Write_Data), .en(x31), .clk(clk), .Q(x31o));  // open: clr

  // Other names for the same wires on the sheet: read_data1[31:0] = Read_Data_1; read_data2[31:0] = Read_Data_2;
  //   read_reg1[4:0] = rs1; read_reg2[4:0] = rs2; write_en = RegWEn; write_reg[4:0] = rd; x1o[31:0] = ra;
  //   x2o[31:0] = sp; x5o[31:0] = t0; x6o[31:0] = t1; x7o[31:0] = t2; x8o[31:0] = s0; x9o[31:0] = s1; x10o[31:0] = a0

  // Notes on the sheet:
  //   INPUTS to your circuit
  //   DON'T CHANGE THE LOCATIONS OF THE INPUTS AND OUTPUTS!
  //   These are DEBUG/TEST outputs from your circuit.
  //   OUTPUTS from your circuit
endmodule
